// Logisim project ULA.circ as structural Verilog
module HalfSum (
  input  A,
  input  B,
  output Sum,
  output CarryOut
);

  and and_1 (CarryOut, A, B);
  xor xor_1 (Sum, B, A);
endmodule

module FullSum (
  input  A,
  input  B,
  input  CarryIn,
  output Sum,
  output CarryOut
);

  wire halfsum_1_carryout, halfsum_1_sum, halfsum_2_carryout;

  HalfSum halfsum_1 (.A(A), .B(B), .Sum(halfsum_1_sum), .CarryOut(halfsum_1_carryout));
  HalfSum halfsum_2 (.A(halfsum_1_sum), .B(CarryIn), .Sum(Sum), .CarryOut(halfsum_2_carryout));
  OR or_1 (.A(halfsum_2_carryout), .B(halfsum_1_carryout), .Out(CarryOut));
endmodule

module XOR (
  input  A,
  input  B,
  output Out
);

  wire and_1_out, and_2_out, not_1_out, not_2_out;

  and and_1 (and_1_out, A, not_1_out);
  not not_1 (not_1_out, B);
  not not_2 (not_2_out, A);
  and and_2 (and_2_out, not_2_out, B);
  OR or_1 (.A(and_1_out), .B(and_2_out), .Out(Out));
endmodule

module OR (
  input  A,
  input  B,
  output Out
);

  wire and_1_out, not_1_out, not_2_out;

  not not_1 (not_1_out, A);
  not not_2 (not_2_out, B);
  not not_3 (Out, and_1_out);
  and and_1 (and_1_out, not_1_out, not_2_out);
endmodule

module Sum (
  input  [15:0] A,
  input  [15:0] B,
  input  CarryIn,
  output CarryOut,
  output [15:0] Sum
);

  wire fullsum_1_carryout, fullsum_2_carryout, fullsum_3_carryout, fullsum_4_carryout, fullsum_5_carryout,
       fullsum_7_carryout, fullsum_8_carryout, fullsum_9_carryout, fullsum_10_carryout, fullsum_11_carryout,
       fullsum_12_carryout, fullsum_13_carryout, fullsum_14_carryout, fullsum_15_carryout,
       fullsum_16_carryout;

  FullSum fullsum_1 (.A(fullsum_14_carryout), .B(B[10]), .CarryIn(A[10]), .Sum(Sum[10]), .CarryOut(fullsum_1_carryout));
  FullSum fullsum_2 (.A(fullsum_1_carryout), .B(B[11]), .CarryIn(A[11]), .Sum(Sum[11]), .CarryOut(fullsum_2_carryout));
  FullSum fullsum_3 (.A(fullsum_2_carryout), .B(B[12]), .CarryIn(A[12]), .Sum(Sum[12]), .CarryOut(fullsum_3_carryout));
  FullSum fullsum_4 (.A(fullsum_3_carryout), .B(B[13]), .CarryIn(A[13]), .Sum(Sum[13]), .CarryOut(fullsum_4_carryout));
  FullSum fullsum_5 (.A(fullsum_4_carryout), .B(B[14]), .CarryIn(A[14]), .Sum(Sum[14]), .CarryOut(fullsum_5_carryout));
  FullSum fullsum_6 (.A(fullsum_5_carryout), .B(B[15]), .CarryIn(A[15]), .Sum(Sum[15]), .CarryOut(CarryOut));
  FullSum fullsum_7 (.A(fullsum_16_carryout), .B(B[2]), .CarryIn(A[2]), .Sum(Sum[2]), .CarryOut(fullsum_7_carryout));
  FullSum fullsum_8 (.A(fullsum_7_carryout), .B(B[3]), .CarryIn(A[3]), .Sum(Sum[3]), .CarryOut(fullsum_8_carryout));
  FullSum fullsum_9 (.A(fullsum_8_carryout), .B(B[4]), .CarryIn(A[4]), .Sum(Sum[4]), .CarryOut(fullsum_9_carryout));
  FullSum fullsum_10 (.A(fullsum_9_carryout), .B(B[5]), .CarryIn(A[5]), .Sum(Sum[5]), .CarryOut(fullsum_10_carryout));
  FullSum fullsum_11 (.A(fullsum_10_carryout), .B(B[6]), .CarryIn(A[6]), .Sum(Sum[6]), .CarryOut(fullsum_11_carryout));
  FullSum fullsum_12 (.A(fullsum_11_carryout), .B(B[7]), .CarryIn(A[7]), .Sum(Sum[7]), .CarryOut(fullsum_12_carryout));
  FullSum fullsum_13 (.A(fullsum_12_carryout), .B(B[8]), .CarryIn(A[8]), .Sum(Sum[8]), .CarryOut(fullsum_13_carryout));
  FullSum fullsum_14 (.A(fullsum_13_carryout), .B(B[9]), .CarryIn(A[9]), .Sum(Sum[9]), .CarryOut(fullsum_14_carryout));
  FullSum fullsum_15 (.A(CarryIn), .B(B[0]), .CarryIn(A[0]), .Sum(Sum[0]), .CarryOut(fullsum_15_carryout));
  FullSum fullsum_16 (.A(fullsum_15_carryout), .B(B[1]), .CarryIn(A[1]), .Sum(Sum[1]), .CarryOut(fullsum_16_carryout));
endmodule

module ULA (
  input  [15:0] A,
  input  [15:0] B,
  input  [3:0] Op,
  output [15:0] Result,
  output Estouro_Aritimetico,
  output Comparacao
);

  wire Carry_Adder, Carry_Divider, Carry_Multiplier, Carry_Subtractor;
  wire [15:0] Output_Adder, Output_AND, Output_Divider, Output_Multiplier, Output_NAND, Output_Negator,
       Output_NOR, Output_OR, Output_Shifter, Output_Subtractor;

  Adder #(.width(16)) adder_1 (.a(A), .b(B), .out(Output_Adder), .cout(Carry_Adder));  // open: cin
  Subtractor #(.width(16)) subtractor_1 (.a(A), .b(B), .out(Output_Subtractor), .bout(Carry_Subtractor));  // open: bin
  assign Output_AND = A & B;  // AND_Gate and_1, 16 bits wide
  Shifter #(.width(16)) shifter_1 (.in(A), .\dist (B[3:0]), .out(Output_Shifter));
  assign Output_NAND = ~(A & B);  // NAND_Gate nand_1, 16 bits wide
  Multiplier #(.width(16)) multiplier_1 (.a(A), .b(B), .out(Output_Multiplier));  // open: cin, cout
  Divider #(.width(16)) divider_1 (.a(A), .b(B), .out(Output_Divider));  // open: upper, rem
  assign Output_OR = A | B;  // OR_Gate or_1, 16 bits wide
  Negator #(.width(16)) negator_1 (.in(A), .out(Output_Negator));
  assign Output_NOR = ~(A | B);  // NOR_Gate nor_1, 16 bits wide
  Multiplexer #(.select(4), .width(16)) multiplexer_1 (
    .in0(Output_AND), .in1(Output_Subtractor), .in2(Output_Multiplier), .in3(Output_Divider),
    .in4(Output_NAND), .in11(Output_NOR), .in12(Output_Shifter), .in13(Output_Adder), .in14(Output_Negator),
    .in15(Output_OR), .out(Result), .sel(Op));  // open: in5, in6, in7, in8, in9, in10, en
  Multiplexer #(.select(4)) multiplexer_2 (
    .in1(Carry_Subtractor), .in2(Carry_Multiplier), .in3(Carry_Divider), .in13(Carry_Adder),
    .out(Estouro_Aritimetico), .sel(Op));  // open: in0, in4, in5, in6, in7, in8, in9, in10, in11, in12, in14, in15, en
  Comparator #(.width(16)) comparator_1 (.a(A), .b(B), .gt(Comparacao));  // open: eq, lt
endmodule
